// Logisim project lucas.circ as structural Verilog: 2 circuits, main circuit main
module main (
  input  A,
  input  B,
  input  A_2,
  input  B_2,
  input  C,
  input  C_2,
  output Vai_1,
  output Vai_1_2,
  output S,
  output S_2
);

  marea marea_1 (.S(S), .Vai_1(Vai_1), .A(A), .B(C), .C(B));
  marea marea_2 (.S(S_2), .Vai_1(Vai_1_2), .A(A_2), .B(C_2), .C(B_2));
endmodule

module marea (
  input  A,
  input  B,
  input  C,
  output S,
  output Vai_1
);

  wire and_1_out, and_2_out, or_1_out, xor_1_out;

  xor xor_1 (xor_1_out, C, B);
  or or_1 (or_1_out, C, B);
  xor xor_2 (S, xor_1_out, A);
  and and_1 (and_1_out, or_1_out, A);
  and and_2 (and_2_out, C, B);
  or or_2 (Vai_1, and_1_out, and_2_out);
endmodule
