// Logisim project lucas3.circ as structural Verilog: 6 circuits, main circuit main
module main (
  input  A,
  input  B,
  input  A_2,
  input  B_2,
  input  C,
  input  C_2,
  input  [1:0] xy,
  input  [3:0] b_3,
  input  [3:0] a_3,
  output Vai_1,
  output Vai_1_2,
  output S,
  output S_2,
  output Overflow,
  output [3:0] out_15,
  output [3:0] out_16,
  output [3:0] out_17,
  output Overflow_2
);

  Add_1 add_1_1 (.S(S), .Vai_1(Vai_1), .A(A), .B(C), .C(B));
  Add_4 add_4_1 (.B(a_3), .A(b_3), .Overflow(Overflow), .S(out_16));
  Sub_4 sub_4_1 (.in_1(a_3), .out_4(out_17), .out_3(Overflow_2), .in_2(b_3));
  Rot_esq rot_esq_1 (.abcd(a_3), .xy(xy), .abcd_2(out_15));
  Add_1 add_1_2 (.S(S_2), .Vai_1(Vai_1_2), .A(A_2), .B(C_2), .C(B_2));
endmodule

module Add_1 (
  input  A,
  input  B,
  input  C,
  output S,
  output Vai_1
);

  wire and_1_out, and_2_out, or_1_out, xor_1_out;

  xor xor_1 (xor_1_out, C, B);
  or or_1 (or_1_out, C, B);
  xor xor_2 (S, xor_1_out, A);
  and and_1 (and_1_out, or_1_out, A);
  and and_2 (and_2_out, C, B);
  or or_2 (Vai_1, and_1_out, and_2_out);
endmodule

module Add_4 (
  input  [3:0] A,
  input  [3:0] B,
  output Overflow,
  output [3:0] S
);

  wire add_1_2_vai_1, add_1_3_vai_1, add_1_4_vai_1;

  // Probe on A
  Add_1 add_1_1 (.S(S[3]), .Vai_1(Overflow), .A(A[3]), .B(add_1_2_vai_1), .C(B[3]));
  Add_1 add_1_2 (.S(S[2]), .Vai_1(add_1_2_vai_1), .A(A[2]), .B(add_1_3_vai_1), .C(B[2]));
  Add_1 add_1_3 (.S(S[1]), .Vai_1(add_1_3_vai_1), .A(A[1]), .B(add_1_4_vai_1), .C(B[1]));
  Add_1 add_1_4 (.S(S[0]), .Vai_1(add_1_4_vai_1), .A(A[0]), .B(1'b0), .C(B[0]));
  // Probe on S
  // Probe on B
endmodule

module Sub_1 (
  input  A,
  input  B,
  input  C,
  output S,
  output Vai_1
);

  wire and_1_out, and_2_out, or_1_out, xor_1_out;

  xor xor_1 (xor_1_out, C, B);
  or or_1 (or_1_out, C, B);
  xor xor_2 (S, xor_1_out, A);
  and and_1 (and_1_out, or_1_out, ~A);  // AND_Gate
  and and_2 (and_2_out, C, B);
  or or_2 (Vai_1, and_1_out, and_2_out);
endmodule

module Sub_4 (
  input  [3:0] in_1,
  input  [3:0] in_2,
  output out_3,
  output [3:0] out_4
);

  wire sub_1_2_vai_1, sub_1_3_vai_1, sub_1_4_vai_1;

  // Probe on in_1
  Sub_1 sub_1_1 (.S(out_4[3]), .Vai_1(out_3), .A(in_1[3]), .B(sub_1_2_vai_1), .C(in_2[3]));
  Sub_1 sub_1_2 (.S(out_4[2]), .Vai_1(sub_1_2_vai_1), .A(in_1[2]), .B(sub_1_3_vai_1), .C(in_2[2]));
  // Probe on sub_1_4_vai_1
  Sub_1 sub_1_3 (.S(out_4[1]), .Vai_1(sub_1_3_vai_1), .A(in_1[1]), .B(sub_1_4_vai_1), .C(in_2[1]));
  // Probe on out_4
  Sub_1 sub_1_4 (.S(out_4[0]), .Vai_1(sub_1_4_vai_1), .A(in_1[0]), .B(1'b0), .C(in_2[0]));
  // Probe on in_2
endmodule

module Rot_esq (
  input  [1:0] xy,
  input  [3:0] abcd,
  output [3:0] abcd_2
);

  wire and_1_out, and_2_out, and_3_out, and_4_out, and_5_out, and_6_out, and_7_out, and_8_out, and_9_out;

  and and_1 (and_1_out, ~xy[1], ~xy[0], abcd[3]);  // AND_Gate
  and and_2 (and_2_out, ~xy[1], xy[0], abcd[2]);  // AND_Gate
  and and_3 (and_3_out, xy[1], ~xy[0], abcd[1]);  // AND_Gate
  and and_4 (and_4_out, xy[1], xy[0], abcd[0]);
  and and_5 (and_5_out, ~xy[1], ~xy[0], abcd[2]);  // AND_Gate
  and and_6 (and_6_out, xy[0], abcd[2]);  // AND_Gate
  and and_7 (and_7_out, xy[1], ~xy[0], abcd[0]);  // AND_Gate
  and and_8 (and_8_out, ~xy[1], ~xy[0], abcd[1]);  // AND_Gate
  and and_9 (and_9_out, ~xy[1], xy[0], abcd[0]);  // AND_Gate
  and and_10 (abcd_2[0], ~xy[1], ~xy[0], abcd[0]);  // AND_Gate
  or or_1 (abcd_2[2], and_5_out, and_6_out, and_7_out);
  or or_2 (abcd_2[3], and_1_out, and_2_out, and_3_out, and_4_out);
  or or_3 (abcd_2[1], and_8_out, and_9_out);
endmodule
